// Logisim project DLD PROJECT.circ as structural Verilog: 1 circuit, main circuit main
module main (
  input  Code__1,
  input  Code_2,
  input  Code__3,
  input  Code__4,
  input  Input__1,
  input  Input_2,
  input  Input_3,
  input  Input__4,
  output Output
);

  wire xnor_1_out, xnor_2_out, xnor_3_out, xnor_4_out;

  xnor xnor_1 (xnor_1_out, Code__1, Input__1);
  xnor xnor_2 (xnor_2_out, Code_2, Input_2);
  xnor xnor_3 (xnor_3_out, Code__3, Input_3);
  xnor xnor_4 (xnor_4_out, Code__4, Input__4);
  and and_1 (Output, xnor_1_out, xnor_2_out, xnor_3_out, xnor_4_out);
endmodule
